# Fritzing sketch electronic_design (saved by Fritzing 0.9.9b)
breadboards: 1

parts:
  J1 = Basic Servo
  J2 = Basic Servo
  M3 = gear-motor
  Part2 = Motor Driver 1A Dual TB6612FNG
  M4 = gear-motor
  Part3 = Adafruit MAX98357A I2S 3W Class D Amplifier [part_number="Adafruit #3006"]
  HC-SR04_Sensor_1 = HC-SR04 Ultrasonic Distance Sensor
  U1 = LIPO-2000mAh [package=lipo-2000]
  Part6 = Breakout Board for Electret Microphone
  BAT1 = BC9VPC [package=bc9vpc]  # not connected
  M5 = fc-51 [package=THT]
  M6 = fc-51 [package=THT]
  U2 = TCM8240MD [package=tcm8240md]  # not connected
  Jetson_Nano1 = jetsonnano
  SPKR1 = Loudspeaker
  LCD2 = TFT 1.8 inch 160x128 w SD

nets:
  GND: J1.gnd, J2.gnd, Part3.GND, HC-SR04_Sensor_1.GND, Part6.GND, M5.pin2, M6.pin2, Jetson_Nano1.connector37, LCD2.pin2
  VCC: J1.vcc, J2.vcc, Part2.VCC, Part3.VIN, HC-SR04_Sensor_1.VCC, Part6.VCC, M5.pin3, M6.pin3, Jetson_Nano1.connector38, LCD2.pin_1, LCD2.pin_8
  N1: J1.pulse, Jetson_Nano1.connector31
  N2: J2.pulse, Jetson_Nano1.connector9
  N3: M3.pin_1, Part2.A02
  N4: M3.pin_2, Part2.A01
  N5: Part2.GND, U1.-
  N6: Part2.B01, M4.pin_1
  N7: Part2.B02, M4.pin_2
  N8: Part2.VM, U1.+
  N9: Part2.PWMA, Jetson_Nano1.connector15
  N10: Part2.AIN2, Jetson_Nano1.connector21
  N11: Part2.AIN1, Jetson_Nano1.connector17
  N12: Part2.STBY, Jetson_Nano1.connector20
  N13: Part2.BIN1, Jetson_Nano1.connector16
  N14: Part2.BIN2, Jetson_Nano1.connector24
  N15: Part2.PWMB, Jetson_Nano1.connector18
  N16: Part3.DIN, Jetson_Nano1.connector14
  N17: Part3.BCLK, Jetson_Nano1.connector27
  N18: Part3.LRCLK, Jetson_Nano1.connector7
  N19: Part3.VO-, SPKR1.pin1
  N20: Part3.VO+, SPKR1.pin2
  N21: HC-SR04_Sensor_1.TRIG, Jetson_Nano1.connector3
  N22: HC-SR04_Sensor_1.ECHO, Jetson_Nano1.connector5
  N23: Part6.AUD, Jetson_Nano1.connector28
  N24: M5.pin1, Jetson_Nano1.connector6
  N25: M6.pin1, Jetson_Nano1.connector32
  N26: Jetson_Nano1.connector1, LCD2.pin3
  N27: Jetson_Nano1.connector2, LCD2.pin_6
  N28: Jetson_Nano1.connector10, LCD2.pin_7
  N29: Jetson_Nano1.connector35, LCD2.pin_5
  N30: Jetson_Nano1.connector36, LCD2.pin4

custom parts:
  Adafruit MAX98357A I2S 3W Class D Amplifier: Listen to this good news - we now have an all in one digital audio amp breakout board that works incredibly well with the Raspberry Pi! If you're looking for an easy and low cost way to get you digital sound files bumpin' then the MAX08357 I2S Amp Breakout is for you. It takes standard I2S digital audio input and, not only decodes it into analog, but also amplifies it directly into a speaker.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
  TFT 1.8 inch 160x128 w SD: This is a generic 1.8 tft spi lcd display available on ebay and others. The 1.8" display has 128x160 color pixels and in this version pin names in breadboard (unlike the real board).
